// Logisim project miniARM_IO.circ as structural Verilog: 1 circuit, main circuit main
module main (
);

  wire and_1_out, and_2_out, and_3_out, and_4_out, Clear_screen_out, comparator_1_eq, comparator_2_eq,
       comparator_3_eq, comparator_4_eq, comparator_5_eq, comparator_6_eq, comparator_7_eq,
       control_unit_1_p1, control_unit_1_p10, HPC, HR, HRADM, HRI, HSR, MemB, not_1_out, not_2_out,
       not_3_out, not_4_out, not_6_out, PCA, register_file_1_p8, Reset_PC_out, Reset_Registers_out, RW;
  wire [1:0] RI_q;
  wire [2:0] Rx, Ry, Rz;
  wire [3:0] SR_q, undriven;
  wire [3:1] CodeUAL;
  wire [4:0] OpCode;
  wire [6:0] keyboard_1_data;
  wire [14:0] RADM_q_2;
  wire [15:0] controlled_buffer_1_out, controlled_buffer_2_out, controlled_buffer_3_out,
       controlled_buffer_7_out, controlled_buffer_8_out, divider_1_out, divider_1_rem, LHS_q,
       multiplier_1_out, PC_q, ram_1_data, register_file_1_p5, register_file_1_p6, register_file_1_p7, RHS_q;
  wire [15:15] RADM_q;

  Register #(.width(16)) RADM (.D(register_file_1_p6), .Q({RADM_q[15], RADM_q_2}), .clk(HRADM));  // open: en, clr
  assign controlled_buffer_1_out = MemB ? controlled_buffer_2_out : 16'bz;  // Controlled_Buffer controlled_buffer_1
  RAM #(.addrWidth(16), .dataWidth(16), .bus("separate")) ram_1 (
    .addr({1'b0, RADM_q_2}), .din(register_file_1_p6), .data(ram_1_data), .clk(RW));  // open: str, sel, ld, clr
  assign controlled_buffer_2_out = not_1_out ? ram_1_data : 16'bz;  // Controlled_Buffer controlled_buffer_2
  not not_1 (not_1_out, RADM_q[15]);
  Register #(.width(16)) RI (.D(controlled_buffer_2_out), .Q({OpCode, Rx, Ry, Rz, RI_q}), .clk(HRI));  // open: en, clr
  not not_2 (not_2_out, RW);
  and and_1 (and_1_out, not_2_out, comparator_1_eq);
  Keyboard keyboard_1 (.clk(and_1_out), .data(keyboard_1_data));  // open: re, clr, avail
  assign controlled_buffer_3_out = PCA ? PC_q : 16'bz;  // Controlled_Buffer controlled_buffer_3
  Register #(.width(16)) PC (.D(register_file_1_p6), .Q(PC_q), .clk(HPC), .clr(Reset_PC_out));  // open: en
  Button Reset_PC (.out(Reset_PC_out));
  Comparator #(.width(16), .mode("unsigned")) comparator_1 (
    .a({RADM_q[15], RADM_q_2}), .b(16'h9234), .eq(comparator_1_eq));  // open: gt, lt
  assign controlled_buffer_2_out = comparator_1_eq ? {{9{1'b0}}, keyboard_1_data} : 16'bz;  // Controlled_Buffer controlled_buffer_4
  assign controlled_buffer_3_out = not_3_out ? register_file_1_p5 : 16'bz;  // Controlled_Buffer controlled_buffer_5
  assign controlled_buffer_1_out = not_4_out ? register_file_1_p7 : 16'bz;  // Controlled_Buffer controlled_buffer_6
  not not_3 (not_3_out, PCA);
  not not_4 (not_4_out, MemB);
  // Register_File register_file_1: pin names not known; wires that end beside it: Ry, Rz, Rx, HR, register_file_1_p5, register_file_1_p6, register_file_1_p7, register_file_1_p8, CodeUAL[1], controlled_buffer_3_out, CodeUAL[2], CodeUAL[3]
  not not_5 (register_file_1_p8, Reset_Registers_out);
  Button Reset_Registers (.out(Reset_Registers_out));
  Comparator #(.width(16), .mode("unsigned")) comparator_2 (
    .a({RADM_q[15], RADM_q_2}), .b(16'habcd), .eq(comparator_2_eq));  // open: gt, lt
  not not_6 (not_6_out, RW);
  TTY tty_1 (.data(register_file_1_p6[6:0]), .clk(and_2_out), .clr(Clear_screen_out));  // open: we
  and and_2 (and_2_out, comparator_2_eq, not_6_out);
  // ALU alu_1: pin names not known; wires that end beside it: register_file_1_p6, undriven[3], controlled_buffer_1_out, undriven[2], undriven[1]
  // Control_Unit control_unit_1: pin names not known; wires that end beside it: control_unit_1_p1, HRADM, HRI, HR, HSR, HPC, RW, PCA, MemB, control_unit_1_p10, control_unit_1_p10
  Register #(.width(4)) SR (.D(undriven), .Q(SR_q), .clk(HSR));  // open: en, clr
  Button Clear_screen (.out(Clear_screen_out));
  Clock clock_1 (.out(control_unit_1_p1));
  Comparator #(.width(16), .mode("unsigned")) comparator_3 (
    .a({RADM_q[15], RADM_q_2}), .b(16'haaab), .eq(comparator_3_eq));  // open: gt, lt
  assign controlled_buffer_7_out = comparator_3_eq ? register_file_1_p6 : 16'bz;  // Controlled_Buffer controlled_buffer_7
  Register #(.width(16)) RHS (.D(controlled_buffer_7_out), .Q(RHS_q), .clk(and_3_out));  // open: en, clr
  and and_3 (and_3_out, comparator_3_eq, ~RW);  // AND_Gate
  Comparator #(.width(16), .mode("unsigned")) comparator_4 (
    .a({RADM_q[15], RADM_q_2}), .b(16'haaaa), .eq(comparator_4_eq));  // open: gt, lt
  assign controlled_buffer_8_out = comparator_4_eq ? register_file_1_p6 : 16'bz;  // Controlled_Buffer controlled_buffer_8
  and and_4 (and_4_out, comparator_4_eq, ~RW);  // AND_Gate
  Register #(.width(16)) LHS (.D(controlled_buffer_8_out), .Q(LHS_q), .clk(and_4_out));  // open: en, clr
  Comparator #(.width(16), .mode("unsigned")) comparator_5 (
    .a({RADM_q[15], RADM_q_2}), .b(16'haaac), .eq(comparator_5_eq));  // open: gt, lt
  Multiplier #(.width(16)) multiplier_1 (.a(LHS_q), .b(RHS_q), .out(multiplier_1_out));  // open: cin, cout
  assign controlled_buffer_2_out = comparator_5_eq ? multiplier_1_out : 16'bz;  // Controlled_Buffer controlled_buffer_9
  assign controlled_buffer_2_out = comparator_6_eq ? divider_1_out : 16'bz;  // Controlled_Buffer controlled_buffer_10
  Comparator #(.width(16), .mode("unsigned")) comparator_6 (
    .a({RADM_q[15], RADM_q_2}), .b(16'haaad), .eq(comparator_6_eq));  // open: gt, lt
  Divider #(.width(16)) divider_1 (.a(LHS_q), .b(RHS_q), .out(divider_1_out), .rem(divider_1_rem));  // open: upper
  assign controlled_buffer_2_out = comparator_7_eq ? divider_1_rem : 16'bz;  // Controlled_Buffer controlled_buffer_11
  Comparator #(.width(16), .mode("unsigned")) comparator_7 (
    .a({RADM_q[15], RADM_q_2}), .b(16'haaae), .eq(comparator_7_eq));  // open: gt, lt

  // Notes on the sheet:
  //   Mémoire
  //   Entrée : clavier
  //   Sortie : Terminal
  //   données W
  //   adresses
  //   données R
endmodule
